// Logisim project JKMestreEscravo.circ as structural Verilog
module numeros (
  input  in_1,
  output [3:0] out_2
);

  wire button_1_out, button_2_out, clock_1_out;

  Clock clock_1 (.out(clock_1_out));
  Button button_1 (.out(button_1_out));
  Button button_2 (.out(button_2_out));
  JKME jkme_1 (.Cock(clock_1_out), .J(in_1), .Set(button_1_out), .Reset(button_2_out), .Q(out_2[0]));  // open: NQ
  JKME jkme_2 (.Cock(out_2[0]), .J(in_1), .Set(button_1_out), .Reset(button_2_out), .Q(out_2[1]));  // open: NQ
  JKME jkme_3 (.Cock(out_2[1]), .J(in_1), .Set(button_1_out), .Reset(button_2_out), .Q(out_2[2]));  // open: NQ
  JKME jkme_4 (.Cock(out_2[2]), .J(in_1), .Set(button_1_out), .Reset(button_2_out), .Q(out_2[3]));  // open: NQ
  Hex_Digit_Display hex_digit_display_1 (.value(out_2));  // open: dp
endmodule

module JKME (
  input  Set,
  input  J,
  input  Cock,
  input  Reset,
  output Q,
  output NQ
);

  wire nand_1_out, nand_2_out, nand_3_out, nand_4_out, nand_5_out, nand_6_out, not_1_out, not_2_out,
       not_3_out;

  nand nand_1 (nand_1_out, J, Cock, NQ);
  nand nand_2 (nand_2_out, Q, Cock, J);
  not not_1 (not_1_out, Reset);
  not not_2 (not_2_out, Set);
  nand nand_3 (nand_3_out, not_2_out, nand_1_out, nand_4_out);
  nand nand_4 (nand_4_out, nand_3_out, nand_2_out, not_1_out);
  not not_3 (not_3_out, Cock);
  nand nand_5 (nand_5_out, nand_3_out, not_3_out);
  nand nand_6 (nand_6_out, nand_4_out, not_3_out);
  nand nand_7 (Q, not_2_out, nand_5_out, NQ);
  nand nand_8 (NQ, Q, nand_6_out, not_1_out);
endmodule
