// Logisim project somador_4_bits_com_vhdl.circ as structural Verilog
module meiaSoma (
  input  A,
  input  B,
  input  cin,
  output S,
  output cout
);

  wire and_1_out, and_2_out, xor_1_out;

  xor xor_1 (xor_1_out, A, cin);
  and and_1 (and_1_out, A, cin);
  xor xor_2 (S, xor_1_out, B);
  and and_2 (and_2_out, xor_1_out, B);
  or or_1 (cout, and_2_out, and_1_out);
endmodule

module somador_4_bits (
  input  A3,
  input  A2,
  input  A1,
  input  A0,
  input  B3,
  input  B2,
  input  B1,
  input  B0,
  output out_9,
  output out_10,
  output out_11,
  output out_12,
  output out_13
);

  wire meiasoma_1_cout, meiasoma_2_cout, meiasoma_3_cout;

  meiaSoma meiasoma_1 (.A(A0), .B(B0), .cin(1'b0), .S(out_13), .cout(meiasoma_1_cout));
  meiaSoma meiasoma_2 (.A(A1), .B(B1), .cin(meiasoma_1_cout), .S(out_12), .cout(meiasoma_2_cout));
  meiaSoma meiasoma_3 (.A(A2), .B(B2), .cin(meiasoma_2_cout), .S(out_11), .cout(meiasoma_3_cout));
  meiaSoma meiasoma_4 (.A(A3), .B(B3), .cin(meiasoma_3_cout), .S(out_10), .cout(out_9));
endmodule

module somador_e_vhdl (
  input  A3,
  input  A2,
  input  A1,
  input  A0,
  input  B3,
  input  B2,
  input  B1,
  input  B0,
  output out_9,
  output out_10,
  output out_11,
  output out_12,
  output ov,
  output [3:0] out_14,
  output out_15
);

  somador_4_bits somador_4_bits_1 (
    .A3(A3), .A2(A2), .A1(A1), .A0(A0), .B3(B3), .B2(B2), .B1(B1), .B0(B0), .out_9(out_9), .out_10(out_10),
    .out_11(out_11), .out_12(out_12), .out_13(ov));
  somador_vhdl somador_vhdl_1 (.A({A3, A2, A1, A0}), .B({B3, B2, B1, B0}), .S(out_14), .ov(out_15));
endmodule

// VHDL entity somador_vhdl, as the project stores it:
LIBRARY ieee;
USE ieee.std_logic_1164.all;

ENTITY somador_vhdl IS
  PORT (
  ------------------------------------------------------------------------------
  --Insert input ports below
    A      : IN  std_logic_vector(3 DOWNTO 0);                   -- input bit example
    B       : IN  std_logic_vector(3 DOWNTO 0); -- input vector example
  ------------------------------------------------------------------------------
  --Insert output ports below
                  -- output bit example
    S        : OUT std_logic_vector(3 DOWNTO 0);
    ov    : OUT std_logic
    );
END somador_vhdl;


--------------------------------------------------------------------------------
--Complete your VHDL description below
--------------------------------------------------------------------------------

ARCHITECTURE TypeArchitecture OF somador_vhdl IS
signal carry : std_logic_vector(3 DOWNTO 0);
BEGIN
S(0) <= A(0) xor B(0);
carry(1) <= A(0) and B(0);
S(1) <= ((A(1) xor carry(1)) xor B(1));
carry(2) <= ((A(1) xor carry(1)) and B(1)) or carry(1);
S(2) <= ((A(2) xor carry(2)) xor B(2));
carry(3) <= ((A(2) xor carry(2)) and B(2)) or carry(2);
S(3) <= ((A(3) xor carry(3)) xor B(3));
ov <= ((A(3) xor carry(3)) and B(3)) or carry(3);


END TypeArchitecture;
