// Logisim project Mux.circ as structural Verilog: 21 circuits, main circuit main
module main (
  input  [3:0] A,
  input  [3:0] B,
  input  in_3,
  input  in_4,
  input  in_5,
  output [4:0] out_6,
  output [3:0] out_7,
  output [3:0] out_8,
  output [3:0] out_9,
  output [3:0] out_10,
  output [3:0] out_11,
  output [3:0] out_12,
  output out_13,
  output out_14
);

  wire [3:0] demux3_1_a0, demux3_1_a1, demux3_1_a2, demux3_1_a5, demux3_1_a7, demux3_1_b0, demux3_1_b1,
       demux3_1_b2;

  Demux3 demux3_1 (
    .A(A), .B(B), .in_3(in_3), .in_4(in_4), .in_5(in_5), .A0(demux3_1_a0), .B0(demux3_1_b0),
    .A1(demux3_1_a1), .B1(demux3_1_b1), .A2(demux3_1_a2), .B2(demux3_1_b2), .A3(out_8), .B3(out_9),
    .A4(out_11), .B4(out_12), .A5(demux3_1_a5), .A7(demux3_1_a7));  // open: B5, A6, B6, B7
  somador_4_bits somador_4_bits_1 (.A(demux3_1_a0), .B(demux3_1_b0), .out_3(out_6));
  sub_com_vhl_e_sem sub_com_vhl_e_sem_1 (.in_1(demux3_1_a1), .in_2(demux3_1_b1), .out_3(out_7));
  sumSubCompleto sumsubcompleto_1 (.A(demux3_1_a2), .B(demux3_1_b2), .S(out_10));
  DetectorDeParidade detectordeparidade_1 (.A(demux3_1_a5), .S(out_13));
  DetectorDeZero detectordezero_1 (.in_1(demux3_1_a7), .out_2(out_14));
  MUX3 mux3_1 ();  // open: A, B, C, D, E, F, G, H, SEL1, SEL2, SEL3, out_12
endmodule

module MUX (
  input  in_1,
  input  in_2,
  input  in_3,
  output out_4
);

  wire and_1_out, and_2_out, not_1_out;

  not not_1 (not_1_out, in_3);
  and and_1 (and_1_out, in_1, not_1_out);
  and and_2 (and_2_out, in_2, in_3);
  or or_1 (out_4, and_1_out, and_2_out);
endmodule

module MUX2 (
  input  A,
  input  B,
  input  C,
  input  D,
  input  SEL1,
  input  SEL2,
  output S
);

  wire mux_1_out_4, mux_2_out_4;

  MUX mux_1 (.in_1(A), .in_2(B), .in_3(SEL1), .out_4(mux_1_out_4));
  MUX mux_2 (.in_1(C), .in_2(D), .in_3(SEL1), .out_4(mux_2_out_4));
  MUX mux_3 (.in_1(mux_1_out_4), .in_2(mux_2_out_4), .in_3(SEL2), .out_4(S));
endmodule

module MUX3 (
  input  A,
  input  B,
  input  C,
  input  D,
  input  E,
  input  F,
  input  G,
  input  H,
  input  SEL1,
  input  SEL2,
  input  SEL3,
  output out_12
);

  wire mux2_1_s, mux2_2_s;

  MUX2 mux2_1 (.A(A), .B(B), .C(C), .D(D), .SEL1(SEL1), .SEL2(SEL2), .S(mux2_1_s));
  MUX2 mux2_2 (.A(E), .B(F), .C(G), .D(H), .SEL1(SEL1), .SEL2(SEL2), .S(mux2_2_s));
  MUX mux_1 (.in_1(mux2_1_s), .in_2(mux2_2_s), .in_3(SEL3), .out_4(out_12));
endmodule

module Demux (
  input  [3:0] A,
  input  [3:0] B,
  input  Sel,
  output [3:0] out_4,
  output [3:0] out_5,
  output [3:0] out_6,
  output [3:0] out_7
);

  assign out_4 = ~{4{Sel}} & B;  // AND_Gate and_1, 4 bits wide
  assign out_5 = ~{4{Sel}} & A;  // AND_Gate and_2, 4 bits wide
  assign out_6 = B & {4{Sel}};  // AND_Gate and_3, 4 bits wide
  assign out_7 = A & {4{Sel}};  // AND_Gate and_4, 4 bits wide
endmodule

module Demux2 (
  input  [3:0] A,
  input  [3:0] B,
  input  Sel1,
  input  Sel2,
  output [3:0] A0,
  output [3:0] B0,
  output [3:0] A1,
  output [3:0] B1,
  output [3:0] A2,
  output [3:0] B2,
  output [3:0] A3,
  output [3:0] B3
);

  wire [3:0] demux_1_out_4, demux_1_out_5, demux_1_out_6, demux_1_out_7;

  Demux demux_1 (
    .A(A), .B(B), .Sel(Sel1), .out_4(demux_1_out_4), .out_5(demux_1_out_5), .out_6(demux_1_out_6),
    .out_7(demux_1_out_7));
  Demux demux_2 (.A(demux_1_out_4), .B(demux_1_out_5), .Sel(Sel2), .out_4(A0), .out_5(B0), .out_6(A1), .out_7(B1));
  Demux demux_3 (.A(demux_1_out_6), .B(demux_1_out_7), .Sel(Sel2), .out_4(A2), .out_5(B2), .out_6(A3), .out_7(B3));
endmodule

module Demux3 (
  input  [3:0] A,
  input  [3:0] B,
  input  in_3,
  input  in_4,
  input  in_5,
  output [3:0] A0,
  output [3:0] B0,
  output [3:0] A1,
  output [3:0] B1,
  output [3:0] A2,
  output [3:0] B2,
  output [3:0] A3,
  output [3:0] B3,
  output [3:0] A4,
  output [3:0] B4,
  output [3:0] A5,
  output [3:0] B5,
  output [3:0] A6,
  output [3:0] B6,
  output [3:0] A7,
  output [3:0] B7
);

  wire [3:0] demux2_1_a0, demux2_1_a3, demux2_1_b0, demux2_1_b3;

  Demux2 demux2_1 (
    .A(A), .B(B), .Sel1(in_3), .Sel2(in_3), .A0(demux2_1_a0), .B0(demux2_1_b0), .A3(demux2_1_a3),
    .B3(demux2_1_b3));  // open: A1, B1, A2, B2
  Demux2 demux2_2 (
    .A(demux2_1_a0), .B(demux2_1_b0), .Sel1(in_4), .Sel2(in_5), .A0(A0), .B0(B0), .A1(A1), .B1(B1), .A2(A2),
    .B2(B2), .A3(A3), .B3(B3));
  Demux2 demux2_3 (
    .A(demux2_1_a3), .B(demux2_1_b3), .Sel1(in_4), .Sel2(in_5), .A0(A4), .B0(B4), .A1(A5), .B1(B5), .A2(A6),
    .B2(B6), .A3(A7), .B3(B7));
endmodule

module meiaSoma (
  input  A,
  input  B,
  input  cin,
  output S,
  output cout
);

  wire and_1_out, and_2_out, xor_1_out;

  xor xor_1 (xor_1_out, A, cin);
  and and_1 (and_1_out, A, cin);
  xor xor_2 (S, xor_1_out, B);
  and and_2 (and_2_out, xor_1_out, B);
  or or_1 (cout, and_2_out, and_1_out);
endmodule

module somador_4_bits (
  input  [3:0] A,
  input  [3:0] B,
  output [4:0] out_3
);

  wire meiasoma_1_cout, meiasoma_2_cout, meiasoma_3_cout;

  meiaSoma meiasoma_1 (.A(A[0]), .B(B[0]), .cin(1'b0), .S(out_3[0]), .cout(meiasoma_1_cout));
  meiaSoma meiasoma_2 (.A(A[1]), .B(B[1]), .cin(meiasoma_1_cout), .S(out_3[1]), .cout(meiasoma_2_cout));
  meiaSoma meiasoma_3 (.A(A[2]), .B(B[2]), .cin(meiasoma_2_cout), .S(out_3[2]), .cout(meiasoma_3_cout));
  meiaSoma meiasoma_4 (.A(A[3]), .B(B[3]), .cin(meiasoma_3_cout), .S(out_3[3]), .cout(out_3[4]));
endmodule

module sumSubCompleto (
  input  [3:0] A,
  input  [3:0] B,
  output [3:0] S
);

  wire complemento_1_out_5, complemento_1_out_6, complemento_1_out_7, complemento_1_out_8;

  Complemento complemento_1 (
    .in_1(B[0]), .in_2(B[1]), .in_3(B[2]), .in_4(B[3]), .out_5(complemento_1_out_5),
    .out_6(complemento_1_out_6), .out_7(complemento_1_out_7), .out_8(complemento_1_out_8));
  fullSum4Bits fullsum4bits_1 (
    .A0(A[0]), .A1(A[1]), .A2(A[2]), .A3(A[3]), .B0(complemento_1_out_5), .B1(complemento_1_out_6),
    .B2(complemento_1_out_7), .B3(complemento_1_out_8), .S0(S[0]), .S1(S[1]), .S2(S[2]), .S3(S[3]));
endmodule

module meioSum (
  input  A,
  input  B,
  output S,
  output Carry
);

  xor xor_1 (S, A, B);
  and and_1 (Carry, A, B);
endmodule

module Complemento (
  input  in_1,
  input  in_2,
  input  in_3,
  input  in_4,
  output out_5,
  output out_6,
  output out_7,
  output out_8
);

  wire not_1_out, not_2_out, not_3_out, not_4_out;

  not not_1 (not_1_out, in_1);
  not not_2 (not_2_out, in_2);
  not not_3 (not_3_out, in_3);
  not not_4 (not_4_out, in_4);
  fullSum4Bits fullsum4bits_1 (
    .A0(not_1_out), .A1(not_2_out), .A2(not_3_out), .A3(not_4_out), .B0(1'b1), .B1(1'b0), .B2(1'b0),
    .B3(1'b0), .S0(out_5), .S1(out_6), .S2(out_7), .S3(out_8));
endmodule

module fullSum (
  input  A,
  input  B,
  input  Cin,
  output S,
  output C
);

  wire meiosum_1_carry, meiosum_1_s, meiosum_2_carry;

  meioSum meiosum_1 (.A(A), .B(Cin), .S(meiosum_1_s), .Carry(meiosum_1_carry));
  meioSum meiosum_2 (.A(meiosum_1_s), .B(B), .S(S), .Carry(meiosum_2_carry));
  or or_1 (C, meiosum_1_carry, meiosum_2_carry);
endmodule

module fullSum4Bits (
  input  A0,
  input  A1,
  input  A2,
  input  A3,
  input  B0,
  input  B1,
  input  B2,
  input  B3,
  output S0,
  output S1,
  output S2,
  output S3
);

  wire fullsum_1_c, fullsum_2_c, fullsum_3_c;

  fullSum fullsum_1 (.A(A0), .B(B0), .Cin(1'b0), .S(S0), .C(fullsum_1_c));
  fullSum fullsum_2 (.A(A1), .B(B1), .Cin(fullsum_1_c), .S(S1), .C(fullsum_2_c));
  fullSum fullsum_3 (.A(A2), .B(B2), .Cin(fullsum_2_c), .S(S2), .C(fullsum_3_c));
  fullSum fullsum_4 (.A(A3), .B(B3), .Cin(fullsum_3_c), .S(S3));  // open: C
endmodule

module meioSubComplementos (
  input  in_1,
  input  in_2,
  input  in_3,
  output out_4,
  output out_5
);

  wire not_1_out, xor_1_out;

  xor xor_1 (xor_1_out, in_2, not_1_out);
  not not_1 (not_1_out, in_3);
  or or_1 (out_4, in_1, xor_1_out);
  and and_1 (out_5, in_1, xor_1_out);
endmodule

module meio_sub (
  input  E,
  input  Cin,
  output S,
  output Cout
);

  wire not_1_out;

  not not_1 (not_1_out, E);
  xor xor_1 (S, E, Cin);
  and and_1 (Cout, Cin, not_1_out);
endmodule

module sub_1_bit (
  input  A,
  input  B,
  input  cin,
  output S,
  output cout
);

  wire meio_sub_1_cout, meio_sub_1_s, meio_sub_2_cout;

  meio_sub meio_sub_1 (.E(A), .Cin(cin), .S(meio_sub_1_s), .Cout(meio_sub_1_cout));
  meio_sub meio_sub_2 (.E(meio_sub_1_s), .Cin(B), .S(S), .Cout(meio_sub_2_cout));
  or or_1 (cout, meio_sub_2_cout, meio_sub_1_cout);
endmodule

module sub_4_bits (
  input  A3,
  input  A2,
  input  A1,
  input  A0,
  input  B3,
  input  B2,
  input  B1,
  input  B0,
  output S3,
  output S2,
  output S1,
  output S0
);

  wire sub_1_bit_1_cout, sub_1_bit_2_cout, sub_1_bit_3_cout;

  sub_1_bit sub_1_bit_1 (.A(A0), .B(B0), .cin(1'b0), .S(S0), .cout(sub_1_bit_1_cout));
  sub_1_bit sub_1_bit_2 (.A(A1), .B(B1), .cin(sub_1_bit_1_cout), .S(S1), .cout(sub_1_bit_2_cout));
  sub_1_bit sub_1_bit_3 (.A(A2), .B(B2), .cin(sub_1_bit_2_cout), .S(S2), .cout(sub_1_bit_3_cout));
  sub_1_bit sub_1_bit_4 (.A(A3), .B(B3), .cin(sub_1_bit_3_cout), .S(S3));  // open: cout
endmodule

module sub_com_vhl_e_sem (
  input  [3:0] in_1,
  input  [3:0] in_2,
  output [3:0] out_3
);

  sub_4_bits sub_4_bits_1 (
    .A3(in_1[3]), .A2(in_1[2]), .A1(in_1[1]), .A0(in_1[0]), .B3(in_2[3]), .B2(in_2[2]), .B1(in_2[1]),
    .B0(in_2[0]), .S3(out_3[3]), .S2(out_3[2]), .S1(out_3[1]), .S0(out_3[0]));
endmodule

module DetectorDeZero (
  input  [3:0] in_1,
  output out_2
);

  wire or_1_out;

  or or_1 (or_1_out, in_1[0], in_1[1], in_1[2], in_1[3]);
  not not_1 (out_2, or_1_out);
endmodule

module DetectorDeParidade (
  input  [3:0] A,
  output S
);

  wire and_1_out, and_2_out, and_3_out, and_4_out, and_5_out, and_6_out, and_7_out, and_8_out, not_1_out,
       not_2_out, not_3_out, not_4_out;

  not not_1 (not_1_out, A[0]);
  not not_2 (not_2_out, A[1]);
  not not_3 (not_3_out, A[2]);
  not not_4 (not_4_out, A[3]);
  and and_1 (and_1_out, not_1_out, not_2_out, not_3_out, not_4_out);
  and and_2 (and_2_out, not_1_out, not_2_out, A[2], A[3]);
  and and_3 (and_3_out, not_1_out, A[1], not_3_out, A[3]);
  and and_4 (and_4_out, not_1_out, A[1], A[2], not_4_out);
  and and_5 (and_5_out, A[0], not_2_out, not_3_out, A[3]);
  and and_6 (and_6_out, A[0], not_2_out, A[2], not_4_out);
  and and_7 (and_7_out, A[0], A[1], not_3_out, not_4_out);
  and and_8 (and_8_out, A[0], A[1], A[2], A[3]);
  or or_1 (S, and_1_out, and_2_out, and_3_out, and_4_out, and_5_out, and_6_out, and_7_out, and_8_out);
endmodule
