// Logisim project TrabalhoFinal1Completo.circ as structural Verilog
module main (
  input  [3:0] A,
  input  [3:0] B,
  input  in_3,
  input  [2:0] Sel,
  output out_5,
  output [3:0] out_6
);

  wire a_t, and_1_out, and_2_out, and_3_out, and_4_out, b_t, bihex_1_a, bihex_1_b, bihex_1_c, bihex_1_d,
       bihex_1_e, bihex_1_f, bihex_1_g, bihex_2_a, bihex_2_b, bihex_2_c, bihex_2_d, bihex_2_e, bihex_2_f,
       bihex_2_g, c, d, e, f, g, not_1_out, not_2_out, not_3_out, not_4_out, not_5_out, not_6_out, not_7_out,
       not_8_out, not_9_out, not_10_out, not_11_out, not_12_out, not_13_out, not_14_out, not_15_out,
       not_16_out, not_17_out, not_18_out, not_19_out, not_20_out, seletordisplay_1_out_3;
  wire [3:0] and_5_out;
  wire [3:3] seletordisplay_1_out_2;

  BiHex bihex_1 (
    .Entrada(B), .a(bihex_1_a), .b(bihex_1_b), .c(bihex_1_c), .d(bihex_1_d), .e(bihex_1_e), .f(bihex_1_f),
    .g(bihex_1_g));
  BiHex bihex_2 (
    .Entrada(A), .a(bihex_2_a), .b(bihex_2_b), .c(bihex_2_c), .d(bihex_2_d), .e(bihex_2_e), .f(bihex_2_f),
    .g(bihex_2_g));
  _7_Segment_Display u_7_segment_display_1 (
    .g(bihex_1_g), .f(bihex_1_f), .a(bihex_1_a), .b(bihex_1_b), .e(bihex_1_e), .d(bihex_1_d), .c(bihex_1_c));  // open: dp
  _7_Segment_Display u_7_segment_display_2 (
    .g(bihex_2_g), .f(bihex_2_f), .a(bihex_2_a), .b(bihex_2_b), .e(bihex_2_e), .d(bihex_2_d), .c(bihex_2_c));  // open: dp
  and and_1 (and_1_out, seletordisplay_1_out_3, out_6[3]);
  not not_1 (not_1_out, and_1_out);
  not not_2 (not_2_out, and_1_out);
  _7_Segment_Display u_7_segment_display_3 (
    .g(1'b0), .f(not_1_out), .a(not_2_out), .b(1'b1), .e(not_3_out), .d(not_4_out), .c(1'b1));  // open: dp
  not not_3 (not_3_out, and_1_out);
  not not_4 (not_4_out, and_1_out);
  and and_2 (and_2_out, seletordisplay_1_out_3, out_6[2]);
  not not_5 (not_5_out, and_2_out);
  not not_6 (not_6_out, and_2_out);
  _7_Segment_Display u_7_segment_display_4 (
    .g(1'b0), .f(not_5_out), .a(not_6_out), .b(1'b1), .e(not_7_out), .d(not_8_out), .c(1'b1));  // open: dp
  not not_7 (not_7_out, and_2_out);
  not not_8 (not_8_out, and_2_out);
  and and_3 (and_3_out, seletordisplay_1_out_3, out_6[1]);
  not not_9 (not_9_out, and_3_out);
  not not_10 (not_10_out, and_3_out);
  _7_Segment_Display u_7_segment_display_5 (
    .g(1'b0), .f(not_9_out), .a(not_10_out), .b(1'b1), .e(not_11_out), .d(not_12_out), .c(1'b1));  // open: dp
  _7_Segment_Display u_7_segment_display_6 (
    .g(1'b0), .f(not_14_out), .a(not_15_out), .b(1'b1), .e(not_13_out), .d(not_16_out), .c(1'b1));  // open: dp
  not not_11 (not_11_out, and_3_out);
  not not_12 (not_12_out, and_3_out);
  not not_13 (not_13_out, and_4_out);
  TrabalhoFinal1 trabalhofinal1_1 (.A(A), .B(B), .Enable(in_3), .Sel(Sel), .OV(out_5), .S(out_6));
  seletorDisplay seletordisplay_1 (.in_1(Sel), .out_2(seletordisplay_1_out_2[3]), .out_3(seletordisplay_1_out_3));
  and and_4 (and_4_out, seletordisplay_1_out_3, out_6[0]);
  not not_14 (not_14_out, and_4_out);
  not not_15 (not_15_out, and_4_out);
  not not_16 (not_16_out, and_4_out);
  assign and_5_out = {4{seletordisplay_1_out_2[3]}} & out_6;  // AND_Gate and_5, 4 bits wide
  not not_17 (not_17_out, out_5);
  not not_18 (not_18_out, out_5);
  _7_Segment_Display u_7_segment_display_7 (
    .g(1'b0), .f(not_17_out), .a(not_18_out), .b(1'b1), .e(not_19_out), .d(not_20_out), .c(1'b1));  // open: dp
  not not_19 (not_19_out, out_5);
  not not_20 (not_20_out, out_5);
  BiHex bihex_3 (.Entrada(and_5_out), .a(a_t), .b(b_t), .c(c), .d(d), .e(e), .f(f), .g(g));
  _7_Segment_Display u_7_segment_display_8 (.g(g), .f(f), .a(a_t), .b(b_t), .e(e), .d(d), .c(c));  // open: dp

  // Notes on the sheet:
  //   000 soma
  //   001 subtração
  //   010 sub por complemento
  //   011 and
  //   100 or
  //   101 comparador
  //   110 deslocamento
  //   111 detector de zero
endmodule

module main_VHDL (
  input  [3:0] A,
  input  [3:0] B,
  input  in_3,
  input  [2:0] Sel,
  output out_5,
  output [3:0] out_6
);

  wire a_t, and_1_out, and_2_out, and_3_out, and_4_out, b_t, bihex_1_a, bihex_1_b, bihex_1_c, bihex_1_d,
       bihex_1_e, bihex_1_f, bihex_1_g, bihex_2_a, bihex_2_b, bihex_2_c, bihex_2_d, bihex_2_e, bihex_2_f,
       bihex_2_g, c, d, e, f, g, not_1_out, not_2_out, not_3_out, not_4_out, not_5_out, not_6_out, not_7_out,
       not_8_out, not_9_out, not_10_out, not_11_out, not_12_out, not_13_out, not_14_out, not_15_out,
       not_16_out, not_17_out, not_18_out, not_19_out, not_20_out, seletor_display_vhdl_1_y;
  wire [3:0] and_5_out;
  wire [3:3] seletor_display_vhdl_1_x;

  BiHex bihex_1 (
    .Entrada(B), .a(bihex_1_a), .b(bihex_1_b), .c(bihex_1_c), .d(bihex_1_d), .e(bihex_1_e), .f(bihex_1_f),
    .g(bihex_1_g));
  BiHex bihex_2 (
    .Entrada(A), .a(bihex_2_a), .b(bihex_2_b), .c(bihex_2_c), .d(bihex_2_d), .e(bihex_2_e), .f(bihex_2_f),
    .g(bihex_2_g));
  _7_Segment_Display u_7_segment_display_1 (
    .g(bihex_1_g), .f(bihex_1_f), .a(bihex_1_a), .b(bihex_1_b), .e(bihex_1_e), .d(bihex_1_d), .c(bihex_1_c));  // open: dp
  _7_Segment_Display u_7_segment_display_2 (
    .g(bihex_2_g), .f(bihex_2_f), .a(bihex_2_a), .b(bihex_2_b), .e(bihex_2_e), .d(bihex_2_d), .c(bihex_2_c));  // open: dp
  and and_1 (and_1_out, seletor_display_vhdl_1_y, out_6[3]);
  not not_1 (not_1_out, and_1_out);
  not not_2 (not_2_out, and_1_out);
  _7_Segment_Display u_7_segment_display_3 (
    .g(1'b0), .f(not_1_out), .a(not_2_out), .b(1'b1), .e(not_3_out), .d(not_4_out), .c(1'b1));  // open: dp
  not not_3 (not_3_out, and_1_out);
  not not_4 (not_4_out, and_1_out);
  and and_2 (and_2_out, seletor_display_vhdl_1_y, out_6[2]);
  not not_5 (not_5_out, and_2_out);
  not not_6 (not_6_out, and_2_out);
  _7_Segment_Display u_7_segment_display_4 (
    .g(1'b0), .f(not_5_out), .a(not_6_out), .b(1'b1), .e(not_7_out), .d(not_8_out), .c(1'b1));  // open: dp
  not not_7 (not_7_out, and_2_out);
  not not_8 (not_8_out, and_2_out);
  and and_3 (and_3_out, seletor_display_vhdl_1_y, out_6[1]);
  not not_9 (not_9_out, and_3_out);
  not not_10 (not_10_out, and_3_out);
  _7_Segment_Display u_7_segment_display_5 (
    .g(1'b0), .f(not_9_out), .a(not_10_out), .b(1'b1), .e(not_11_out), .d(not_12_out), .c(1'b1));  // open: dp
  not not_11 (not_11_out, and_3_out);
  not not_12 (not_12_out, and_3_out);
  TrabalhoFinal1 trabalhofinal1_1 (.A(A), .B(B), .Enable(in_3), .Sel(Sel), .OV(out_5), .S(out_6));
  seletor_display_VHDL seletor_display_vhdl_1 (.a(Sel), .x(seletor_display_vhdl_1_x[3]), .y(seletor_display_vhdl_1_y));
  and and_4 (and_4_out, seletor_display_vhdl_1_y, out_6[0]);
  not not_13 (not_13_out, and_4_out);
  not not_14 (not_14_out, and_4_out);
  _7_Segment_Display u_7_segment_display_6 (
    .g(1'b0), .f(not_13_out), .a(not_14_out), .b(1'b1), .e(not_15_out), .d(not_16_out), .c(1'b1));  // open: dp
  not not_15 (not_15_out, and_4_out);
  not not_16 (not_16_out, and_4_out);
  assign and_5_out = {4{seletor_display_vhdl_1_x[3]}} & out_6;  // AND_Gate and_5, 4 bits wide
  not not_17 (not_17_out, out_5);
  not not_18 (not_18_out, out_5);
  _7_Segment_Display u_7_segment_display_7 (
    .g(1'b0), .f(not_17_out), .a(not_18_out), .b(1'b1), .e(not_19_out), .d(not_20_out), .c(1'b1));  // open: dp
  not not_19 (not_19_out, out_5);
  not not_20 (not_20_out, out_5);
  BiHex bihex_3 (.Entrada(and_5_out), .a(a_t), .b(b_t), .c(c), .d(d), .e(e), .f(f), .g(g));
  _7_Segment_Display u_7_segment_display_8 (.g(g), .f(f), .a(a_t), .b(b_t), .e(e), .d(d), .c(c));  // open: dp

  // Notes on the sheet:
  //   001 subtração
  //   010 sub por complemento
  //   011 and
  //   100 or
  //   101 comparador
  //   110 deslocamento
  //   111 detector de zero
endmodule

module TrabalhoFinal1 (
  input  [3:0] A,
  input  [3:0] B,
  input  Enable,
  input  [2:0] Sel,
  output OV,
  output [3:0] S
);

  wire demux3_1_s0, demux3_1_s1, demux3_1_s2, demux3_1_s3, demux3_1_s4, demux3_1_s5, demux3_1_s6, demux3_1_s7;
  wire [3:0] andenabler_1_out_4, comparadorenabler_1_out_4, deslocamento_1_s, detectordezero_1_s,
       orenabler_1_out_4, somador_4_bits_enable_1_out_4, subcomplementoenabler_1_s, subenabler_1_out_4;

  Demux3 demux3_1 (
    .A(Enable), .in_2(Sel), .S0(demux3_1_s0), .S1(demux3_1_s1), .S2(demux3_1_s2), .S3(demux3_1_s3),
    .S4(demux3_1_s4), .S5(demux3_1_s5), .S6(demux3_1_s6), .S7(demux3_1_s7));
  somador_4_bits_enable somador_4_bits_enable_1 (
    .A(A), .B(B), .ENABLER(demux3_1_s0), .out_4(somador_4_bits_enable_1_out_4), .out_5(OV));
  subENABLER subenabler_1 (.A(A), .B(B), .in_3(demux3_1_s1), .out_4(subenabler_1_out_4));
  subComplementoENABLER subcomplementoenabler_1 (.A(A), .B(B), .ENABLER(demux3_1_s2), .S(subcomplementoenabler_1_s));
  andENABLER andenabler_1 (.A(A), .B(B), .ENABLER(demux3_1_s3), .out_4(andenabler_1_out_4));
  ORENABLER orenabler_1 (.A(A), .B(B), .ENABLER(demux3_1_s4), .out_4(orenabler_1_out_4));
  comparadorENABLER comparadorenabler_1 (.A(A), .B(B), .ENABLER(demux3_1_s5), .out_4(comparadorenabler_1_out_4));
  deslocamento deslocamento_1 (.A(A), .B(B), .ENABLER(demux3_1_s6), .S(deslocamento_1_s));
  DetectorDeZero detectordezero_1 (.A(A), .enabler(demux3_1_s7), .S(detectordezero_1_s));
  assign S = somador_4_bits_enable_1_out_4 | subenabler_1_out_4 | subcomplementoenabler_1_s | andenabler_1_out_4 | orenabler_1_out_4 | comparadorenabler_1_out_4 | deslocamento_1_s | detectordezero_1_s;  // OR_Gate or_1, 4 bits wide

  // Notes on the sheet:
  //   000 soma
  //   001 subtração
  //   010 sub por complemento
  //   011 and
  //   100 or
  //   101 comparador
  //   110 deslocamento
  //   111 detector de zero
endmodule

module trabalhoFinal1VHDL (
  input  [3:0] A,
  input  [3:0] B,
  input  Enabler,
  input  [2:0] Sel,
  output [4:0] out_5
);

  wire comparadorvhdl_1_s, demuxvhdl_1_s0, demuxvhdl_1_s1, demuxvhdl_1_s2, demuxvhdl_1_s3, demuxvhdl_1_s4,
       demuxvhdl_1_s5, demuxvhdl_1_s6, demuxvhdl_1_s7, detectordezerovhdl_1_s;
  wire [3:0] andvhdl_1_s, deslocadorvhdl_1_s, orvhdl_1_s, subcomplemento_1_s, subtrator_4_bits_vhdl_1_s;
  wire [4:0] somador_vhdl_1_s;

  DemuxVHDL demuxvhdl_1 (
    .A(Enabler), .Sel(Sel), .S0(demuxvhdl_1_s0), .S1(demuxvhdl_1_s1), .S2(demuxvhdl_1_s2),
    .S3(demuxvhdl_1_s3), .S4(demuxvhdl_1_s4), .S5(demuxvhdl_1_s5), .S6(demuxvhdl_1_s6), .S7(demuxvhdl_1_s7));
  somador_vhdl somador_vhdl_1 (.A(A), .B(B), .ENABLER(demuxvhdl_1_s0), .S(somador_vhdl_1_s));
  subtrator_4_bits_vhdl subtrator_4_bits_vhdl_1 (.A(A), .B(B), .ENABLER(demuxvhdl_1_s1), .S(subtrator_4_bits_vhdl_1_s));
  subComplemento subcomplemento_1 (.A(A), .B(B), .ENABLER(demuxvhdl_1_s2), .S(subcomplemento_1_s));
  andVHDL andvhdl_1 (.A(A), .B(B), .ENABLER(demuxvhdl_1_s3), .S(andvhdl_1_s));
  ORVHDL orvhdl_1 (.A(A), .B(B), .ENABLER(demuxvhdl_1_s4), .S(orvhdl_1_s));
  ComparadorVHDL comparadorvhdl_1 (.A(A), .B(B), .ENABLER(demuxvhdl_1_s5), .S(comparadorvhdl_1_s));
  DeslocadorVHDL deslocadorvhdl_1 (.A(A), .B(B), .C(demuxvhdl_1_s6), .S(deslocadorvhdl_1_s));
  DetectorDeZeroVHDL detectordezerovhdl_1 (.A(A), .ENABLER(demuxvhdl_1_s7), .S(detectordezerovhdl_1_s));
  MuxVHDL muxvhdl_1 (
    .soma(somador_vhdl_1_s), .sub(subtrator_4_bits_vhdl_1_s), .subComp(subcomplemento_1_s),
    .andV(andvhdl_1_s), .orV(orvhdl_1_s), .comparador(comparadorvhdl_1_s), .deslocador(deslocadorvhdl_1_s),
    .detectorZero(detectordezerovhdl_1_s), .sel(Sel), .data_out(out_5));
endmodule

module somador_4_bits_enable (
  input  [3:0] A,
  input  [3:0] B,
  input  ENABLER,
  output [3:0] out_4,
  output out_5
);

  wire [3:0] and_1_out, and_2_out;

  assign and_1_out = A & {4{ENABLER}};  // AND_Gate and_1, 4 bits wide
  assign and_2_out = B & {4{ENABLER}};  // AND_Gate and_2, 4 bits wide
  somador_4_bits somador_4_bits_1 (.A(and_1_out), .B(and_2_out), .S(out_4), .OV(out_5));
endmodule

module subENABLER (
  input  [3:0] A,
  input  [3:0] B,
  input  in_3,
  output [3:0] out_4
);

  wire [3:0] and_1_out, and_2_out;

  assign and_1_out = A & {4{in_3}};  // AND_Gate and_1, 4 bits wide
  assign and_2_out = B & {4{in_3}};  // AND_Gate and_2, 4 bits wide
  sub sub_1 (.A(and_1_out), .B(and_2_out), .out_3(out_4));
endmodule

module subComplementoENABLER (
  input  [3:0] A,
  input  [3:0] B,
  input  ENABLER,
  output [3:0] S
);

  wire [3:0] and_1_out, and_2_out;

  assign and_1_out = A & {4{ENABLER}};  // AND_Gate and_1, 4 bits wide
  assign and_2_out = B & {4{ENABLER}};  // AND_Gate and_2, 4 bits wide
  SubComplemento subcomplemento_1 (.A(and_1_out), .B(and_2_out), .out_3(S));
endmodule

module andENABLER (
  input  [3:0] A,
  input  [3:0] B,
  input  ENABLER,
  output [3:0] out_4
);

  wire [3:0] and_1_out, and_2_out;

  assign and_1_out = A & {4{ENABLER}};  // AND_Gate and_1, 4 bits wide
  assign and_2_out = B & {4{ENABLER}};  // AND_Gate and_2, 4 bits wide
  andy andy_1 (.A(and_1_out), .B(and_2_out), .S(out_4));
endmodule

module ORENABLER (
  input  [3:0] A,
  input  [3:0] B,
  input  ENABLER,
  output [3:0] out_4
);

  wire [3:0] and_1_out, and_2_out;

  assign and_1_out = B & {4{ENABLER}};  // AND_Gate and_1, 4 bits wide
  assign and_2_out = A & {4{ENABLER}};  // AND_Gate and_2, 4 bits wide
  OR2 or2_1 (.A(and_2_out), .B(and_1_out), .out_3(out_4));
endmodule

module comparadorENABLER (
  input  [3:0] A,
  input  [3:0] B,
  input  ENABLER,
  output [3:0] out_4
);

  wire comparador_1_out_3;
  wire [3:0] and_1_out, and_2_out;

  assign and_1_out = {4{ENABLER}} & A;  // AND_Gate and_1, 4 bits wide
  assign and_2_out = B & {4{ENABLER}};  // AND_Gate and_2, 4 bits wide
  Comparador comparador_1 (.A(and_1_out), .B(and_2_out), .out_3(comparador_1_out_3));
  and and_3 (out_4[0], comparador_1_out_3, ENABLER);

  assign out_4[3:1] = 3'b000;
endmodule

module DetectorDeZero (
  input  [3:0] A,
  input  enabler,
  output [3:0] S
);

  wire and_1_out, and_2_out, and_3_out, and_4_out, not_1_out, or_1_out;

  and and_1 (and_1_out, enabler, A[3]);
  and and_2 (and_2_out, enabler, A[2]);
  and and_3 (and_3_out, enabler, A[1]);
  and and_4 (and_4_out, A[0], enabler);
  or or_1 (or_1_out, and_1_out, and_2_out, and_3_out, and_4_out);
  not not_1 (not_1_out, or_1_out);
  and and_5 (S[0], not_1_out, enabler);

  assign S[3:1] = 3'b000;
endmodule

module deslocamento (
  input  [3:0] A,
  input  [3:0] B,
  input  ENABLER,
  output [3:0] S
);

  deslocador deslocador_1 (.A(A), .B(B[1:0]), .Enabler(ENABLER), .out_4(S));
endmodule

module somador_4_bits (
  input  [3:0] A,
  input  [3:0] B,
  output [3:0] S,
  output OV
);

  wire meiasoma_1_cout, meiasoma_2_cout, meiasoma_3_cout;

  meiaSoma meiasoma_1 (.A(A[0]), .B(B[0]), .cin(1'b0), .S(S[0]), .cout(meiasoma_1_cout));
  meiaSoma meiasoma_2 (.A(A[1]), .B(B[1]), .cin(meiasoma_1_cout), .S(S[1]), .cout(meiasoma_2_cout));
  meiaSoma meiasoma_3 (.A(A[2]), .B(B[2]), .cin(meiasoma_2_cout), .S(S[2]), .cout(meiasoma_3_cout));
  meiaSoma meiasoma_4 (.A(A[3]), .B(B[3]), .cin(meiasoma_3_cout), .S(S[3]), .cout(OV));
endmodule

module sub (
  input  [3:0] A,
  input  [3:0] B,
  output [3:0] out_3
);

  sub_4_bits sub_4_bits_1 (.A(A), .B(B), .S(out_3));
endmodule

module OR2 (
  input  [3:0] A,
  input  [3:0] B,
  output [3:0] out_3
);

  assign out_3 = A | B;  // OR_Gate or_1, 4 bits wide
endmodule

module SubComplemento (
  input  [3:0] A,
  input  [3:0] B,
  output [3:0] out_3
);

  wire [3:0] complemento_1_s;

  Complemento complemento_1 (.B(B), .S(complemento_1_s));
  fullSum4Bits fullsum4bits_1 (.in_1(A), .in_2(complemento_1_s), .out_3(out_3));
endmodule

module andy (
  input  [3:0] A,
  input  [3:0] B,
  output [3:0] S
);

  assign S = A & B;  // AND_Gate and_1, 4 bits wide
endmodule

module Comparador (
  input  [3:0] A,
  input  [3:0] B,
  output out_3
);

  wire [3:0] not_1_out, xor_1_out;

  assign xor_1_out = A ^ B;  // XOR_Gate xor_1, 4 bits wide
  assign not_1_out = ~xor_1_out;  // NOT_Gate not_1, 4 bits wide
  and and_1 (out_3, not_1_out[0], not_1_out[1], not_1_out[2], not_1_out[3]);
endmodule

module MUX (
  input  Entrada1,
  input  Entrada2,
  input  in_3,
  output out_4
);

  wire and_1_out, and_2_out;

  and and_1 (and_1_out, Entrada1, ~in_3);  // AND_Gate
  and and_2 (and_2_out, Entrada2, in_3);
  or or_1 (out_4, and_1_out, and_2_out);
endmodule

module MUX2 (
  input  A,
  input  B,
  input  C,
  input  D,
  input  SEL1,
  input  SEL2,
  output S
);

  wire mux_1_out_4, mux_2_out_4;

  MUX mux_1 (.Entrada1(A), .Entrada2(B), .in_3(SEL1), .out_4(mux_1_out_4));
  MUX mux_2 (.Entrada1(C), .Entrada2(D), .in_3(SEL1), .out_4(mux_2_out_4));
  MUX mux_3 (.Entrada1(mux_1_out_4), .Entrada2(mux_2_out_4), .in_3(SEL2), .out_4(S));
endmodule

module MUX3 (
  input  A,
  input  B,
  input  C,
  input  D,
  input  E,
  input  F,
  input  G,
  input  H,
  input  SEL2,
  input  SEL1,
  input  SEL3,
  output out_12
);

  wire mux2_1_s, mux2_2_s;

  MUX2 mux2_1 (.A(A), .B(B), .C(C), .D(D), .SEL1(SEL1), .SEL2(SEL2), .S(mux2_1_s));
  MUX2 mux2_2 (.A(E), .B(F), .C(G), .D(H), .SEL1(SEL1), .SEL2(SEL2), .S(mux2_2_s));
  MUX mux_1 (.Entrada1(mux2_1_s), .Entrada2(mux2_2_s), .in_3(SEL3), .out_4(out_12));
endmodule

module Demux (
  input  A,
  input  Sel,
  output out_3,
  output out_4
);

  and and_1 (out_3, ~Sel, A);  // AND_Gate
  and and_2 (out_4, A, Sel);
endmodule

module Demux2 (
  input  A,
  input  Sel1,
  input  Sel2,
  output A0,
  output B0,
  output A2,
  output B2
);

  wire demux_1_out_3, demux_1_out_4;

  Demux demux_1 (.A(A), .Sel(Sel2), .out_3(demux_1_out_3), .out_4(demux_1_out_4));
  Demux demux_2 (.A(demux_1_out_3), .Sel(Sel1), .out_3(A0), .out_4(B0));
  Demux demux_3 (.A(demux_1_out_4), .Sel(Sel1), .out_3(A2), .out_4(B2));
endmodule

module Demux3 (
  input  A,
  input  [2:0] in_2,
  output S0,
  output S1,
  output S2,
  output S3,
  output S4,
  output S5,
  output S6,
  output S7
);

  wire demux2_1_a0, demux2_1_b2;

  Demux2 demux2_1 (.A(A), .Sel1(in_2[2]), .Sel2(in_2[2]), .A0(demux2_1_a0), .B2(demux2_1_b2));  // open: B0, A2
  Demux2 demux2_2 (.A(demux2_1_a0), .Sel1(in_2[0]), .Sel2(in_2[1]), .A0(S0), .B0(S1), .A2(S2), .B2(S3));
  Demux2 demux2_3 (.A(demux2_1_b2), .Sel1(in_2[0]), .Sel2(in_2[1]), .A0(S4), .B0(S5), .A2(S6), .B2(S7));
endmodule

module meiaSoma (
  input  A,
  input  B,
  input  cin,
  output S,
  output cout
);

  wire and_1_out, and_2_out, xor_1_out;

  xor xor_1 (xor_1_out, A, cin);
  and and_1 (and_1_out, A, cin);
  xor xor_2 (S, xor_1_out, B);
  and and_2 (and_2_out, xor_1_out, B);
  or or_1 (cout, and_2_out, and_1_out);
endmodule

module meio_sub (
  input  E,
  input  Cin,
  output S,
  output Cout
);

  wire not_1_out;

  not not_1 (not_1_out, E);
  xor xor_1 (S, E, Cin);
  and and_1 (Cout, Cin, not_1_out);
endmodule

module sub_1_bit (
  input  A,
  input  B,
  input  cin,
  output S,
  output cout
);

  wire meio_sub_1_cout, meio_sub_1_s, meio_sub_2_cout;

  meio_sub meio_sub_1 (.E(A), .Cin(cin), .S(meio_sub_1_s), .Cout(meio_sub_1_cout));
  meio_sub meio_sub_2 (.E(meio_sub_1_s), .Cin(B), .S(S), .Cout(meio_sub_2_cout));
  or or_1 (cout, meio_sub_2_cout, meio_sub_1_cout);
endmodule

module sub_4_bits (
  input  [3:0] A,
  input  [3:0] B,
  output [3:0] S
);

  wire sub_1_bit_1_cout, sub_1_bit_2_cout, sub_1_bit_3_cout;

  sub_1_bit sub_1_bit_1 (.A(A[0]), .B(B[0]), .cin(1'b0), .S(S[0]), .cout(sub_1_bit_1_cout));
  sub_1_bit sub_1_bit_2 (.A(A[1]), .B(B[1]), .cin(sub_1_bit_1_cout), .S(S[1]), .cout(sub_1_bit_2_cout));
  sub_1_bit sub_1_bit_3 (.A(A[2]), .B(B[2]), .cin(sub_1_bit_2_cout), .S(S[2]), .cout(sub_1_bit_3_cout));
  sub_1_bit sub_1_bit_4 (.A(A[3]), .B(B[3]), .cin(sub_1_bit_3_cout), .S(S[3]));  // open: cout
endmodule

module meioSum (
  input  A,
  input  B,
  output S,
  output Carry
);

  xor xor_1 (S, A, B);
  and and_1 (Carry, A, B);
endmodule

module Complemento (
  input  [3:0] B,
  output [3:0] S
);

  wire [3:0] not_1_out;

  assign not_1_out = ~B;  // NOT_Gate not_1, 4 bits wide
  fullSum4Bits fullsum4bits_1 (.in_1(not_1_out), .in_2(4'b0001), .out_3(S));
endmodule

module fullSum (
  input  A,
  input  B,
  input  Cin,
  output S,
  output C
);

  wire meiosum_1_carry, meiosum_1_s, meiosum_2_carry;

  meioSum meiosum_1 (.A(A), .B(Cin), .S(meiosum_1_s), .Carry(meiosum_1_carry));
  meioSum meiosum_2 (.A(meiosum_1_s), .B(B), .S(S), .Carry(meiosum_2_carry));
  or or_1 (C, meiosum_1_carry, meiosum_2_carry);
endmodule

module fullSum4Bits (
  input  [3:0] in_1,
  input  [3:0] in_2,
  output [3:0] out_3
);

  wire fullsum_1_c, fullsum_2_c, fullsum_3_c;

  fullSum fullsum_1 (.A(in_1[0]), .B(in_2[0]), .Cin(1'b0), .S(out_3[0]), .C(fullsum_1_c));
  fullSum fullsum_2 (.A(in_1[1]), .B(in_2[1]), .Cin(fullsum_1_c), .S(out_3[1]), .C(fullsum_2_c));
  fullSum fullsum_3 (.A(in_1[2]), .B(in_2[2]), .Cin(fullsum_2_c), .S(out_3[2]), .C(fullsum_3_c));
  fullSum fullsum_4 (.A(in_1[3]), .B(in_2[3]), .Cin(fullsum_3_c), .S(out_3[3]));  // open: C
endmodule

module meioSubComplementos (
  input  in_1,
  input  in_2,
  input  in_3,
  output out_4,
  output out_5
);

  wire not_1_out, xor_1_out;

  xor xor_1 (xor_1_out, in_2, not_1_out);
  not not_1 (not_1_out, in_3);
  or or_1 (out_4, in_1, xor_1_out);
  and and_1 (out_5, in_1, xor_1_out);
endmodule

module seletor (
  input  nada,
  input  esquerda,
  input  Direita,
  input  [1:0] B,
  output S
);

  wire and_1_out, and_2_out, and_3_out, not_1_out, not_2_out, not_3_out, not_4_out;

  not not_1 (not_1_out, B[0]);
  not not_2 (not_2_out, B[1]);
  not not_3 (not_3_out, B[0]);
  not not_4 (not_4_out, B[1]);
  and and_1 (and_1_out, not_1_out, nada, not_2_out);
  and and_2 (and_2_out, not_3_out, esquerda, B[1]);
  and and_3 (and_3_out, B[0], Direita, not_4_out);
  or or_1 (S, and_1_out, and_2_out, and_3_out);
endmodule

module seletor_cicuito (
  input  soma,
  input  B,
  input  Deslocar,
  output out_4
);

  wire and_1_out, and_2_out, not_1_out;

  not not_1 (not_1_out, B);
  and and_1 (and_1_out, soma, not_1_out);
  and and_2 (and_2_out, Deslocar, B);
  or or_1 (out_4, and_1_out, and_2_out);
endmodule

module deslocador (
  input  [3:0] A,
  input  [1:0] B,
  input  Enabler,
  output [3:0] out_4
);

  wire and_1_out, and_2_out, and_3_out, and_4_out;

  and and_1 (and_1_out, Enabler, A[3]);
  and and_2 (and_2_out, Enabler, A[2]);
  and and_3 (and_3_out, Enabler, A[1]);
  seletor seletor_1 (.nada(and_1_out), .esquerda(and_2_out), .Direita(1'b0), .B(B), .S(out_4[3]));
  and and_4 (and_4_out, Enabler, A[0]);
  seletor seletor_2 (.nada(and_2_out), .esquerda(and_3_out), .Direita(and_1_out), .B(B), .S(out_4[2]));
  seletor seletor_3 (.nada(and_3_out), .esquerda(and_4_out), .Direita(and_2_out), .B(B), .S(out_4[1]));
  seletor seletor_4 (.nada(and_4_out), .esquerda(1'b0), .Direita(and_3_out), .B(B), .S(out_4[0]));
endmodule

module BiHex (
  input  [3:0] Entrada,
  output a,
  output b,
  output c,
  output d,
  output e,
  output f,
  output g
);

  wire and_1_out, and_2_out, and_3_out, and_4_out, and_5_out, and_6_out, and_7_out, and_8_out, and_9_out,
       and_10_out, and_11_out, and_12_out, and_13_out, and_14_out, and_15_out, and_16_out, and_17_out,
       and_18_out, and_19_out, and_20_out, and_21_out, and_22_out, and_23_out, and_24_out, and_25_out,
       and_26_out, and_27_out, and_28_out, and_29_out, and_30_out, and_31_out, and_32_out, and_33_out,
       and_34_out, and_35_out, not_1_out, not_2_out, not_3_out, not_4_out;

  not not_1 (not_1_out, Entrada[3]);
  not not_2 (not_2_out, Entrada[2]);
  not not_3 (not_3_out, Entrada[1]);
  not not_4 (not_4_out, Entrada[0]);
  and and_1 (and_1_out, not_2_out, not_4_out);
  and and_2 (and_2_out, not_1_out, Entrada[1]);
  and and_3 (and_3_out, not_1_out, Entrada[2], Entrada[0]);
  and and_4 (and_4_out, Entrada[3], not_2_out, not_3_out);
  and and_5 (and_5_out, Entrada[3], not_4_out);
  and and_6 (and_6_out, Entrada[2], Entrada[1]);
  and and_7 (and_7_out, not_1_out, not_3_out, not_4_out);
  and and_8 (and_8_out, not_1_out, Entrada[1], Entrada[0]);
  and and_9 (and_9_out, not_2_out, not_4_out);
  and and_10 (and_10_out, Entrada[3], not_3_out, Entrada[0]);
  and and_11 (and_11_out, not_1_out, not_2_out);
  and and_12 (and_12_out, not_1_out, Entrada[2]);
  and and_13 (and_13_out, Entrada[3], not_2_out);
  and and_14 (and_14_out, not_3_out, Entrada[0]);
  and and_15 (and_15_out, not_2_out, not_3_out);
  and and_16 (and_16_out, not_2_out, Entrada[0]);
  and and_17 (and_17_out, Entrada[2], not_3_out, Entrada[0]);
  and and_18 (and_18_out, not_1_out, not_2_out, not_4_out);
  and and_19 (and_19_out, not_2_out, Entrada[1], Entrada[0]);
  and and_20 (and_20_out, Entrada[3], not_3_out);
  and and_21 (and_21_out, Entrada[2], Entrada[1], not_4_out);
  and and_22 (and_22_out, not_2_out, not_4_out);
  and and_23 (and_23_out, Entrada[1], not_4_out);
  and and_24 (and_24_out, Entrada[3], Entrada[1]);
  and and_25 (and_25_out, Entrada[3], Entrada[2]);
  and and_26 (and_26_out, not_3_out, not_4_out);
  and and_27 (and_27_out, not_1_out, Entrada[2], not_3_out);
  and and_28 (and_28_out, Entrada[2], not_4_out);
  and and_29 (and_29_out, Entrada[3], not_2_out);
  and and_30 (and_30_out, Entrada[3], Entrada[1]);
  and and_31 (and_31_out, not_2_out, Entrada[1]);
  and and_32 (and_32_out, Entrada[3], not_2_out);
  and and_33 (and_33_out, not_1_out, Entrada[2], not_3_out);
  and and_34 (and_34_out, Entrada[1], not_4_out);
  and and_35 (and_35_out, Entrada[3], Entrada[0]);
  or or_1 (a, and_1_out, and_2_out, and_3_out, and_4_out, and_5_out, and_6_out);
  or or_2 (b, and_7_out, and_8_out, and_9_out, and_10_out, and_11_out);
  or or_3 (c, and_12_out, and_13_out, and_14_out, and_15_out, and_16_out);
  or or_4 (d, and_17_out, and_18_out, and_19_out, and_20_out, and_21_out);
  or or_5 (e, and_22_out, and_23_out, and_24_out, and_25_out);
  or or_6 (f, and_26_out, and_27_out, and_28_out, and_29_out, and_30_out);
  or or_7 (g, and_31_out, and_32_out, and_33_out, and_34_out, and_35_out);
endmodule

module ConversorBinario (
  input  in_1
);
endmodule

module seletorDisplay (
  input  [2:0] in_1,
  output out_2,
  output out_3
);

  wire and_1_out, and_2_out, and_3_out, and_4_out, and_5_out, and_6_out, and_7_out, and_8_out;

  and and_1 (and_1_out, ~in_1[2], ~in_1[1], ~in_1[0]);  // AND_Gate
  and and_2 (and_2_out, ~in_1[2], ~in_1[1], in_1[0]);  // AND_Gate
  and and_3 (and_3_out, ~in_1[2], in_1[1], ~in_1[0]);  // AND_Gate
  and and_4 (and_4_out, ~in_1[2], in_1[1], in_1[0]);  // AND_Gate
  and and_5 (and_5_out, in_1[2], ~in_1[1], ~in_1[0]);  // AND_Gate
  and and_6 (and_6_out, in_1[2], ~in_1[1], in_1[0]);  // AND_Gate
  and and_7 (and_7_out, in_1[2], in_1[1], ~in_1[0]);  // AND_Gate
  and and_8 (and_8_out, in_1[2], in_1[1], in_1[0]);
  or or_1 (out_2, and_1_out, and_2_out, and_3_out, and_4_out, and_8_out);
  or or_2 (out_3, and_5_out, and_7_out, and_6_out);

  // Notes on the sheet:
  //   000 soma
  //   001 subtração
  //   010 sub por complemento
  //   011 and
  //   100 or
  //   101 comparador
  //   110 deslocamento
  //   111 detector de zero
endmodule

// VHDL entity somador_vhdl, as the project stores it:
LIBRARY ieee;
USE ieee.std_logic_1164.all;

ENTITY somador_vhdl IS
  PORT (
  ------------------------------------------------------------------------------
  --Insert input ports below
    A      : IN  std_logic_vector(3 DOWNTO 0);                   -- input bit example
    B       : IN  std_logic_vector(3 DOWNTO 0); -- input vector example
    ENABLER: IN std_logic;
  ------------------------------------------------------------------------------
  --Insert output ports below
                  -- output bit example
    S        : OUT std_logic_vector(4 DOWNTO 0)
    
    );
END somador_vhdl;


--------------------------------------------------------------------------------
--Complete your VHDL description below
--------------------------------------------------------------------------------

ARCHITECTURE TypeArchitecture OF somador_vhdl IS
signal carry : std_logic_vector(3 DOWNTO 0);
BEGIN
	process(A, B, ENABLER, carry)
	begin
		if (ENABLER = '1') then
			S(0) <= A(0) xor B(0);
			carry(1) <= A(0) and B(0);
			
			S(1) <= ((A(1) xor carry(1)) xor B(1));
			carry(2) <= (A(1) and carry(1)) or (B(1) and (A(1) xor carry(1)));
			
			S(2) <= ((A(2) xor carry(2)) xor B(2));
			carry(3) <= (A(2) and carry(2)) or (B(2) and (A(2) xor carry(2)));
			
			S(3) <= ((A(3) xor carry(3)) xor B(3));
			S(4) <= (A(3) and carry(3)) or (B(3) and (A(3) xor carry(3)));
		else
		S <= "00000";
		end if;
	end process;

END TypeArchitecture;

// VHDL entity subtrator_4_bits_vhdl, as the project stores it:
LIBRARY ieee;
USE ieee.std_logic_1164.all;

ENTITY subtrator_4_bits_vhdl IS
  PORT (
    A      : IN  std_logic_vector(3 DOWNTO 0); -- vetor de entrada A
    B      : IN  std_logic_vector(3 DOWNTO 0); -- vetor de entrada B
    ENABLER: IN  std_logic;
    S      : OUT std_logic_vector(3 DOWNTO 0)  -- vetor de saída S
  );
END subtrator_4_bits_vhdl;

ARCHITECTURE TypeArchitecture OF subtrator_4_bits_vhdl IS
  SIGNAL borrow : std_logic_vector(4 DOWNTO 0); -- vetores de borrow com bit extra para o último
BEGIN
  PROCESS (A, B, ENABLER, borrow)
  BEGIN
    -- Inicializa o borrow inicial como '0'
    
    
    IF (ENABLER = '1') THEN
    	 borrow(0) <= '0';
      FOR i IN 0 TO 3 LOOP
        S(i) <= A(i) XOR B(i) XOR borrow(i);
        borrow(i+1) <= ((NOT A(i)) AND borrow(i)) OR (((NOT A(i)) XNOR (NOT borrow(i))) AND B(i));
      END LOOP;
    ELSE
      S <= "0000";
    END IF;
  END PROCESS;
END TypeArchitecture;

// VHDL entity subComplemento, as the project stores it:
LIBRARY ieee;
USE ieee.std_logic_1164.all;
USE ieee.numeric_std.all;  -- For operations with unsigned

ENTITY subComplemento IS
  PORT (
    A      : IN  std_logic_vector(3 DOWNTO 0);  -- Input vector A
    B      : IN  std_logic_vector(3 DOWNTO 0);  -- Input vector B
    ENABLER: IN  std_logic;
    S      : OUT std_logic_vector(3 DOWNTO 0)   -- Output (A - B)
  );
END subComplemento;

ARCHITECTURE TypeArchitecture OF subComplemento IS
  signal result : unsigned(4 DOWNTO 0);  -- Result of the addition with an extra bit for carry
  SIGNAL B_complemento : unsigned(4 DOWNTO 0);
  SIGNAL B2 : unsigned(3 DOWNTO 0);
BEGIN
  process(A, B, ENABLER,B_complemento ,B2,result)

    -- Complement of B with extended bit width
  begin
    if (ENABLER = '1') then
      -- Extend and invert B to create the two's complement representation
      B_complemento <= not unsigned('0' & B) + 1;
	 B2 <= B_complemento(3 DOWNTO 0);
      -- Perform A - B using A + B_complemento
      result <= unsigned('0' & A) + unsigned('0' & B2);

      -- Assign the result to S, including the overflow bit
      S <= std_logic_vector(result(3 DOWNTO 0));
    else
      S <= "0000";
    end if;
  end process;
END TypeArchitecture;

// VHDL entity andVHDL, as the project stores it:
LIBRARY ieee;
USE ieee.std_logic_1164.all;

ENTITY andVHDL IS
  PORT (
  ------------------------------------------------------------------------------
  --Insert input ports below
    A        : IN  std_logic_vector(3 DOWNTO 0); -- input vector example
    B        : IN  std_logic_vector(3 DOWNTO 0);
    ENABLER : IN std_logic;
  ------------------------------------------------------------------------------
  --Insert output ports below
    S        : OUT std_logic_vector(3 DOWNTO 0)  -- output vector example
    );
END andVHDL;

--------------------------------------------------------------------------------
--Complete your VHDL description below
--------------------------------------------------------------------------------

ARCHITECTURE TypeArchitecture OF andVHDL IS

BEGIN
 	S<= A and B when ENABLER = '1' else "0000";

END TypeArchitecture;

// VHDL entity ORVHDL, as the project stores it:
LIBRARY ieee;
USE ieee.std_logic_1164.all;

ENTITY ORVHDL IS
  PORT (
  ------------------------------------------------------------------------------
  --Insert input ports below
    A        : IN  std_logic_vector(3 DOWNTO 0); -- input vector example
    B        : IN  std_logic_vector(3 DOWNTO 0);
    ENABLER : IN std_logic;
  ------------------------------------------------------------------------------
  --Insert output ports below
    S        : OUT std_logic_vector(3 DOWNTO 0)  -- output vector example
    );
END ORVHDL;

--------------------------------------------------------------------------------
--Complete your VHDL description below
--------------------------------------------------------------------------------

ARCHITECTURE TypeArchitecture OF ORVHDL IS

BEGIN
 	S<= A or B when ENABLER = '1' else "0000";

END TypeArchitecture;

// VHDL entity ComparadorVHDL, as the project stores it:
--------------------------------------------------------------------------------
-- Project :
-- File    :
-- Autor   :
-- Date    :
--
--------------------------------------------------------------------------------
-- Description :
--
--------------------------------------------------------------------------------

LIBRARY ieee;
USE ieee.std_logic_1164.all;

ENTITY ComparadorVHDL IS
  PORT (
  ------------------------------------------------------------------------------
  --Insert input ports below
    A        : IN  std_logic_vector(3 DOWNTO 0); -- input vector example
    B        : IN  std_logic_vector(3 DOWNTO 0);
    ENABLER : IN std_logic;
  ------------------------------------------------------------------------------
  --Insert output ports below
    S        : OUT std_logic  -- output vector example
    );
END ComparadorVHDL;

--------------------------------------------------------------------------------
--Complete your VHDL description below
--------------------------------------------------------------------------------

ARCHITECTURE TypeArchitecture OF ComparadorVHDL IS
BEGIN
  process(A, B,ENABLER)
  begin
    if A = B  AND ENABLER = '1' then
      S <= '1';  -- Example output when A equals B
    else
      S <= '0';  -- Example output when A does not equal B
    end if;
  end process;
END TypeArchitecture;

// VHDL entity DetectorDeZeroVHDL, as the project stores it:
--------------------------------------------------------------------------------
-- Project :
-- File    :
-- Autor   :
-- Date    :
--
--------------------------------------------------------------------------------
-- Description :
--
--------------------------------------------------------------------------------

LIBRARY ieee;
USE ieee.std_logic_1164.all;

ENTITY DetectorDeZeroVHDL IS
  PORT (
  ------------------------------------------------------------------------------
  --Insert input ports below
    A        : IN  std_logic_vector(3 DOWNTO 0); -- input vector example
    ENABLER : IN std_logic;
  ------------------------------------------------------------------------------
  --Insert output ports below
    S        : OUT std_logic  -- output vector example
    );
END DetectorDeZeroVHDL;

--------------------------------------------------------------------------------
--Complete your VHDL description below
--------------------------------------------------------------------------------

ARCHITECTURE TypeArchitecture OF DetectorDeZeroVHDL IS
BEGIN
  process(A,ENABLER)
  begin
    if A = "0000" AND ENABLER = '1' then
      S <= '1';  -- Example output when A equals B
    else
      S <= '0';  -- Example output when A does not equal B
    end if;
  end process;
END TypeArchitecture;

// VHDL entity DeslocadorVHDL, as the project stores it:
library IEEE;
use IEEE.STD_LOGIC_1164.ALL;
use IEEE.STD_LOGIC_ARITH.ALL;
use IEEE.STD_LOGIC_UNSIGNED.ALL;

entity DeslocadorVHDL is
    Port (
        A : in STD_LOGIC_VECTOR(3 downto 0);
        B : in STD_LOGIC_VECTOR(3 downto 0);
        C : in STD_LOGIC;
        S : out STD_LOGIC_VECTOR(3 downto 0)
    );
end DeslocadorVHDL;

architecture Behavioral of DeslocadorVHDL is
signal B2 : std_logic_vector(1 DOWNTO 0);
begin

    process(A, B, C, B2)
    
    begin
    B2 <= B(1) & B(0);
        if (C = '1') then
            case B2 is
                when "01" =>  -- Deslocamento para a direita
                    S <= '0' & a(3 downto 1);
                when "10" =>  -- Deslocamento para a esquerda
                    S <= a(2 downto 0) & '0';
                when others =>  -- Nenhuma operação
                    S <= A;
            end case;
        else
            S <= (others => '0');  -- Saída 0000 quando C é 0
        end if;
    end process;
end Behavioral;

// VHDL entity DemuxVHDL, as the project stores it:
library IEEE;
use IEEE.STD_LOGIC_1164.ALL;

entity DemuxVHDL is
    Port (
        A : in STD_LOGIC; -- Entrada
        Sel: in STD_LOGIC_VECTOR(2 DOWNTO 0);
        S0 : out STD_LOGIC; -- Saída 0
        S1 : out STD_LOGIC; -- Saída 1
        S2 : out STD_LOGIC; -- Saída 2
        S3 : out STD_LOGIC; -- Saída 3
        S4 : out STD_LOGIC; -- Saída 4
        S5 : out STD_LOGIC; -- Saída 5
        S6 : out STD_LOGIC; -- Saída 6
        S7 : out STD_LOGIC  -- Saída 7
    );
end DemuxVHDL;

architecture Behavioral of DemuxVHDL is
begin
    process(A, Sel)
    begin
    if (A = '1') then
        S0 <= (NOT Sel(2)) AND (NOT Sel(1)) AND (NOT Sel(0));
        S1 <= (NOT Sel(2)) AND (NOT Sel(1)) AND Sel(0);
        S2 <= (NOT Sel(2)) AND Sel(1) AND (NOT Sel(0));
        S3 <= (NOT Sel(2)) AND Sel(1) AND Sel(0);
        S4 <= Sel(2) AND (NOT Sel(1)) AND (NOT Sel(0));
        S5 <= Sel(2) AND (NOT Sel(1)) AND Sel(0);
        S6 <= Sel(2) AND Sel(1) AND (NOT Sel(0));
        S7 <= Sel(2) AND Sel(1) AND Sel(0);
    else
    	   S0 <= '0';
        S1 <= '0';
        S2 <= '0';
        S3 <= '0';
        S4 <= '0';
        S5 <= '0';
        S6 <= '0';
        S7 <= '0';
    end if;
    
    end process;
end Behavioral;

// VHDL entity MuxVHDL, as the project stores it:
LIBRARY ieee;
USE ieee.std_logic_1164.all;

ENTITY MuxVHDL IS
  PORT (
    soma : IN  std_logic_vector(4 DOWNTO 0);
    sub : IN  std_logic_vector(3 DOWNTO 0);
    subComp : IN  std_logic_vector(3 DOWNTO 0);
    andV : IN  std_logic_vector(3 DOWNTO 0);
    orV : IN  std_logic_vector(3 DOWNTO 0);
    comparador : IN  std_logic;
    deslocador : IN  std_logic_vector(3 DOWNTO 0);
    detectorZero : IN  std_logic;
    sel     : IN  std_logic_vector(2 DOWNTO 0); -- 3 bits de seleção
    data_out : OUT std_logic_vector(4 DOWNTO 0)                    -- Saída
  );
END MuxVHDL;

ARCHITECTURE Behavioral OF MuxVHDL IS
BEGIN
  process(soma,sub,subComp,andV,orV,deslocador,comparador,detectorZero,sel)
  begin
    case sel is
      when "000" => data_out <= soma;
      when "001" => data_out <= '0' & sub ;
      when "010" => data_out <= '0' & subComp;
      when "011" => data_out <= '0' & andV;
      when "100" => data_out <= '0' & orV;
      when "101" => data_out <= "0000" & comparador;
      when "110" => data_out <= '0' & deslocador;
      when "111" => data_out <= "0000" & detectorZero;
      when others => data_out <= "00000"; -- Caso indeterminado
    end case;
  end process;
END Behavioral;

// VHDL entity completoVHDL, as the project stores it:
--------------------------------------------------------------------------------
-- Project :
-- File    :
-- Autor   :
-- Date    :
--
--------------------------------------------------------------------------------
-- Description :
--
--------------------------------------------------------------------------------

LIBRARY ieee;
USE ieee.std_logic_1164.all;
USE ieee.numeric_std.all; 

ENTITY completoVHDL IS
  PORT (
  ------------------------------------------------------------------------------
  --Insert input ports below
                        -- input bit example
    A        : IN  std_logic_vector(3 DOWNTO 0);
    B       : IN  std_logic_vector(3 DOWNTO 0);
    -- input vector example
    ENABLER : IN std_logic;
    SEL      : IN  std_logic_vector(2 DOWNTO 0);
  ------------------------------------------------------------------------------
	S       : OUT std_logic_vector(3 DOWNTO 0);
	OV      : OUT std_logic
    );
END completoVHDL;

--------------------------------------------------------------------------------
--Complete your VHDL description below
--------------------------------------------------------------------------------

ARCHITECTURE TypeArchitecture OF completoVHDL IS
signal CARRY : std_logic_vector(3 DOWNTO 0);
SIGNAL B_complemento : unsigned(4 DOWNTO 0);
SIGNAL B2 : unsigned(3 DOWNTO 0);
signal result : unsigned(4 DOWNTO 0);
BEGIN
	PROCESS(A,B,SEL,ENABLER,CARRY,B_complemento,B2,result)
	BEGIN
		OV <= '0';
		S <= "0000";
		IF ENABLER = '1' THEN
			IF (SEL = "000") THEN -- SOMA
				
				S(0) <= A(0) xor B(0);
				carry(1) <= A(0) and B(0);
				
				S(1) <= ((A(1) xor carry(1)) xor B(1));
				carry(2) <= (A(1) and carry(1)) or (B(1) and (A(1) xor carry(1)));
				
				S(2) <= ((A(2) xor carry(2)) xor B(2));
				carry(3) <= (A(2) and carry(2)) or (B(2) and (A(2) xor carry(2)));
				
				S(3) <= ((A(3) xor carry(3)) xor B(3));
				OV <= (A(3) and carry(3)) or (B(3) and (A(3) xor carry(3)));
			ELSIF (SEL = "001") THEN -- SUBTRAÇÃO
				  CARRY(0) <= '0';
                	FOR i IN 0 TO 2 LOOP
	                    S(i) <= A(i) XOR B(i) XOR CARRY(i);
	                    CARRY(i+1) <= ((NOT A(i)) AND CARRY(i)) OR (((NOT A(i)) XNOR (NOT CARRY(i))) AND B(i));
                	END LOOP;
	                S(3) <= A(3) XOR B(3) XOR CARRY(3);
	                OV <= ((NOT A(3)) AND CARRY(3)) OR (((NOT A(3)) XNOR (NOT CARRY(3))) AND B(3));

			ELSIF (SEL = "010") THEN --SUBTRAÇÃO POR COMPLEMENTO
			      B_complemento <= not unsigned('0' & B) + 1;
				 B2 <= B_complemento(3 DOWNTO 0);

			      result <= unsigned('0' & A) + unsigned('0' & B2);
			
			      S <= std_logic_vector(result(3 DOWNTO 0));
			ELSIF (SEL = "011") THEN -- E
				S<= A AND B;
			ELSIF (SEL = "100") THEN -- OU
				S<= A OR B;
			ELSIF (SEL = "101") THEN --COMPARADOR
				IF A = B THEN
				     S <= "0001"; 
    				ELSE
      				S <= "0000";
      			END IF;
			ELSIF (SEL = "110") THEN -- DESLOCADOR
	          	case B(1 downto 0) is
	          		when "00" =>  -- Deslocamento para a esquerda
	                    	S <= A;
	               	when "01" =>  -- Deslocamento para a direita
	               		S <= '0' & a(3 downto 1);
	               	when "10" =>  -- Deslocamento para a esquerda
	                    	S <= a(2 downto 0) & '0';
	               	when others =>  -- Nenhuma operação
	                    	S <= "0000";
		            end case;
			ELSIF (SEL = "111") THEN --DETECTOR DE ZERO
				if A = "0000" then
					S <= "0001";  -- Example output when A equals B
				else
				     S <= "0000";  -- Example output when A does not equal B
				end if;
			END IF;
		END IF;
	END PROCESS;


END TypeArchitecture;

// VHDL entity BiHex_VHDL, as the project stores it:
library IEEE;
use IEEE.STD_LOGIC_1164.ALL;

entity BiHex_VHDL is
    Port (
        AA : in STD_LOGIC;
        BB  : in STD_LOGIC;
        CC  : in STD_LOGIC;
        DD  : in STD_LOGIC;
        a   : out STD_LOGIC;
        b   : out STD_LOGIC;
        c   : out STD_LOGIC;
        d   : out STD_LOGIC;
        e   : out STD_LOGIC;
        f   : out STD_LOGIC;
        g   : out STD_LOGIC
    );
end BiHex_VHDL;

architecture Behavioral of BiHex_VHDL is
begin
    a <= (not BB and not DD) or (not AA and CC) or 
         (not AA and BB and DD) or (AA and not BB and not CC) or (AA and not DD) or 
         (BB and CC);

    b <= (not AA and not CC and not DD) or (not AA and CC and DD) or 
         (not AA and not BB) or (not BB and not DD)or (AA and not CC and DD);

    c <= (not AA and BB) or (AA and not BB) or 
         (not CC and DD) or (not BB and DD) or (not BB and not CC);

    d <= (BB and not CC and DD) or (not AA and not BB and not DD) or 
         (not BB and CC and DD) or (AA and not CC) or 
         (BB and CC and not DD);

    e <= (not BB and not DD) or (CC and not DD) or 
         (AA and CC) or (AA and BB);

    f <= (not CC and not DD) or (not AA and BB and not CC) or 
         (BB and not DD) or (AA and not BB) or (AA and CC);

    g <= (not BB and CC) or (AA and not BB) or 
         (not AA and BB and not CC) or (CC and not DD) or 
         (AA and DD);
end Behavioral;

// VHDL entity seletor_display_VHDL, as the project stores it:
library IEEE;
use IEEE.STD_LOGIC_1164.ALL;

entity seletor_display_VHDL is
    Port (
        a : in STD_LOGIC_VECTOR(2 DOWNTO 0); -- Vetor de entrada (3 bits)
        x : out STD_LOGIC;                  -- Saída x
        y : out STD_LOGIC                   -- Saída y
    );
end seletor_display_VHDL;

architecture Behavioral of seletor_display_VHDL is
begin
    -- Implementação das saídas x e y com base na tabela de verdade
    process(a)
    begin
    	   x <= '0';
    	   y <= '0';
        case a is
            when "000" | "001" | "010" | "101" | "110" | "111" =>
                x <= '1';
                y <= '0';
            when "011" | "100" =>
                x <= '0';
                y <= '1';
            when others =>
                x <= '0';
                y <= '0';
        end case;
    end process;
end Behavioral;
