// Logisim project subComplemento.circ as structural Verilog
module main (
  input  in_1,
  input  in_2,
  input  in_3,
  input  in_4,
  input  in_5,
  input  in_6,
  input  in_7,
  input  in_8,
  output out_9,
  output out_10,
  output out_11,
  output out_12
);

  wire complemento_1_out_5, complemento_1_out_6, complemento_1_out_7, complemento_1_out_8;

  Complemento complemento_1 (
    .in_1(in_5), .in_2(in_6), .in_3(in_7), .in_4(in_8), .out_5(complemento_1_out_5),
    .out_6(complemento_1_out_6), .out_7(complemento_1_out_7), .out_8(complemento_1_out_8));
  fullSum4Bits fullsum4bits_1 (
    .A0(in_1), .A1(in_2), .A2(in_3), .A3(in_4), .B0(complemento_1_out_5), .B1(complemento_1_out_6),
    .B2(complemento_1_out_7), .B3(complemento_1_out_8), .S0(out_9), .S1(out_10), .S2(out_11), .S3(out_12));  // open: Over
endmodule

module meioSum (
  input  A,
  input  B,
  output S,
  output Carry
);

  xor xor_1 (S, A, B);
  and and_1 (Carry, A, B);
endmodule

module Complemento (
  input  in_1,
  input  in_2,
  input  in_3,
  input  in_4,
  output out_5,
  output out_6,
  output out_7,
  output out_8
);

  wire not_1_out, not_2_out, not_3_out, not_4_out;

  not not_1 (not_1_out, in_1);
  not not_2 (not_2_out, in_2);
  not not_3 (not_3_out, in_3);
  not not_4 (not_4_out, in_4);
  fullSum4Bits fullsum4bits_1 (
    .A0(not_1_out), .A1(not_2_out), .A2(not_3_out), .A3(not_4_out), .B0(1'b1), .B1(1'b0), .B2(1'b0),
    .B3(1'b0), .S0(out_5), .S1(out_6), .S2(out_7), .S3(out_8));  // open: Over
endmodule

module fullSum (
  input  A,
  input  B,
  input  Cin,
  output S,
  output C
);

  wire meiosum_1_carry, meiosum_1_s, meiosum_2_carry;

  meioSum meiosum_1 (.A(A), .B(Cin), .S(meiosum_1_s), .Carry(meiosum_1_carry));
  meioSum meiosum_2 (.A(meiosum_1_s), .B(B), .S(S), .Carry(meiosum_2_carry));
  or or_1 (C, meiosum_1_carry, meiosum_2_carry);
endmodule

module fullSum4Bits (
  input  A0,
  input  A1,
  input  A2,
  input  A3,
  input  B0,
  input  B1,
  input  B2,
  input  B3,
  output S0,
  output S1,
  output S2,
  output S3,
  output Over
);

  wire fullsum_1_c, fullsum_2_c, fullsum_3_c;

  fullSum fullsum_1 (.A(A0), .B(B0), .Cin(1'b0), .S(S0), .C(fullsum_1_c));
  fullSum fullsum_2 (.A(A1), .B(B1), .Cin(fullsum_1_c), .S(S1), .C(fullsum_2_c));
  fullSum fullsum_3 (.A(A2), .B(B2), .Cin(fullsum_2_c), .S(S2), .C(fullsum_3_c));
  fullSum fullsum_4 (.A(A3), .B(B3), .Cin(fullsum_3_c), .S(S3), .C(Over));
endmodule

// VHDL entity subComplemento, as the project stores it:
--------------------------------------------------------------------------------
-- Project :
-- File    :
-- Autor   :
-- Date    :
--
--------------------------------------------------------------------------------
-- Description :
--
--------------------------------------------------------------------------------

LIBRARY ieee;
USE ieee.std_logic_1164.all;

ENTITY subComplemento IS
  PORT (
  ------------------------------------------------------------------------------
  --Insert input ports below
    A      : IN  std_logic_vector(3 DOWNTO 0); -- input vector example
  ------------------------------------------------------------------------------
  --Insert output ports below
    B      : OUT std_logic_vector(3 DOWNTO 0)  -- output vector example
    );
END subComplemento;

--------------------------------------------------------------------------------
--Complete your VHDL description below
--------------------------------------------------------------------------------

ARCHITECTURE TypeArchitecture OF subComplemento IS
signal carry : std_logic_vector(3 DOWNTO 0);
BEGIN
	S(0) <= A(0) xor B(0);
	carry(1) <= A(0) and B(0);
	S(1) <= ((A(1) xor carry(1)) xor B(1));
	carry(2) <= ((A(1) xor carry(1)) and B(1)) or carry(1);
	S(2) <= ((A(2) xor carry(2)) xor B(2));
	carry(3) <= ((A(2) xor carry(2)) and B(2)) or carry(2);
	S(3) <= ((A(3) xor carry(3)) xor B(3));
	ov <= ((A(3) xor carry(3)) and B(3)) or carry(3);
END TypeArchitecture;
